# Fritzing sketch pi5_loa (saved by Fritzing 1.0.8)
breadboards: 4

parts:
  RING0 = 24 NeoPixel Ring [part_number=1586]
  A1 = Raspberry Pi 5  # not connected
  J1 = T Cobbler Plus
  Part1 = SPI OLED Monochrome 128x64 0.96 inch
  XC4520_Temp/Humidity = Humidity and Temperature Sensor RHT03
  XC3702_Barometer = Barometric Pressure Sensor - BMP180 Breakout (GY-68)  # not connected
  R3_4_7kΩ_pull-up = 220 Ω Resistor [package=THT]
  PIR_HC-SR501 = LHi958 [package=to-39]
  HC-SR04 = HC-SR04 Ultrasonic Distance Sensor
  R1_1kΩ_divider = Resistor [tolerance=±5% power=0.25W resistance=220 package=THT]
  R2_2_2kΩ_divider = Resistor [tolerance=±5% power=0.25W resistance=220 package=THT]

nets:
  N1: RING0.IN, J1.#19
  VCC: RING0.VDD, J1.5.0V#1, XC4520_Temp/Humidity.Vcc, R3_4_7kΩ_pull-up.Pin_0, PIR_HC-SR501.D, HC-SR04.VCC
  GND: RING0.GND, J1.GND#5, J1.GND#13, Part1.GND, XC4520_Temp/Humidity.GND_1, PIR_HC-SR501.GND, HC-SR04.GND, R2_2_2kΩ_divider.Pin_1
  N2: J1.#4, XC4520_Temp/Humidity.Data-signal, R3_4_7kΩ_pull-up.Pin_1
  N3: J1.#17, PIR_HC-SR501.S
  N4: J1.#23, HC-SR04.TRIG
  3.3V: J1.3.3V, Part1.VDD
  N5: J1.#24, Part1.RES, R1_1kΩ_divider.Pin_1, R2_2_2kΩ_divider.Pin_0
  N6: J1.MOSI, Part1.SDA
  N7: J1.#25, Part1.DC
  N8: J1.SCLK, Part1.SCK
  N9: J1.CE0, Part1.CS
  N10: HC-SR04.ECHO, R1_1kΩ_divider.Pin_0

custom parts:
  Raspberry Pi 5: The RPi5, a faster version of the awesome Raspberry Pi4B ARM Board with 40 pin gpio.
  T Cobbler Plus: The T-Cobbler Plus is an add on prototyping board from Adafruit specifically designed for the Raspberry Pi B+ that can break out all those tasty power, GPIO, I2C and SPI pins from the 40-pin header onto a solderless breadboard. This set will make "cobbling together" prototypes with the Pi super easy. The T-Cobbler Plus can plug into any solderless breadboard.
  SPI OLED Monochrome 128x64 0.96 inch: Unknown 128x64 0.96 inch 128x64 SPI Monochrome OLED display
